# Fritzing sketch BlinkyLoRaWAN (saved by Fritzing 0.9.3b)
breadboards: 1

parts:
  R1 = Resistor [tolerance=±5% resistance=1k package=THT]
  R2 = Resistor [tolerance=±5% resistance=1k package=THT]
  R3 = Resistor [tolerance=±5% resistance=1k package=THT]
  Part1 = Arduino Uno (Rev3)
  LED1 = LED - 5mm [color="Red (633nm)" package="5 mm [THT]"]

nets:
  N1: R1.Pin_0, R2.Pin_0, R3.Pin_0, Part1.GND
  N2: R1.Pin_1, R2.Pin_1, R3.Pin_1, LED1.cathode
  N3: Part1.D3_PWM, LED1.anode
